// Logisim project ALU1Bit.circ as structural Verilog
module ALU (
  input  A,
  input  B,
  input  CarryIn,
  input  BInvert,
  input  AInvert,
  input  [1:0] Operation,
  output Result
);

  wire adder_1_cout, adder_1_out, and_1_out, multiplexer_1_out, multiplexer_2_out, not_1_out, not_2_out,
       or_1_out, xor_1_out;

  not not_1 (not_1_out, A);
  not not_2 (not_2_out, B);
  Multiplexer #(.enable("false")) multiplexer_1 (.in0(A), .in1(not_1_out), .out(multiplexer_1_out), .sel(AInvert));
  Multiplexer #(.enable("false")) multiplexer_2 (.in0(B), .in1(not_2_out), .out(multiplexer_2_out), .sel(BInvert));
  and and_1 (and_1_out, multiplexer_1_out, multiplexer_2_out);
  or or_1 (or_1_out, multiplexer_1_out, multiplexer_2_out);
  xor xor_1 (xor_1_out, multiplexer_1_out, multiplexer_2_out);
  Adder #(.width(1)) adder_1 (
    .a(multiplexer_1_out), .b(multiplexer_2_out), .out(adder_1_out), .cin(CarryIn), .cout(adder_1_cout));
  // Probe on adder_1_cout
  Multiplexer #(.select(2), .enable("false")) multiplexer_3 (
    .in0(and_1_out), .in1(or_1_out), .in2(xor_1_out), .in3(adder_1_out), .out(Result), .sel(Operation));
endmodule
