// Logisim project HazardDetection.circ as structural Verilog: 1 circuit, main circuit main
module main (
  input  MemRead_EX,
  input  [4:0] RS1_ID,
  input  [4:0] RD_EX,
  input  [4:0] RS2_ID,
  input  Branch,
  input  jalr,
  output Stall,
  output Kill
);

  wire comparator_1_eq, comparator_2_eq, or_1_out;

  Comparator #(.width(5)) comparator_1 (.a(RS1_ID), .b(RD_EX), .eq(comparator_1_eq));  // open: gt, lt
  Comparator #(.width(5)) comparator_2 (.a(RS2_ID), .b(RD_EX), .eq(comparator_2_eq));  // open: gt, lt
  or or_1 (or_1_out, comparator_1_eq, comparator_2_eq);
  or or_2 (Kill, Branch, jalr);
  and and_1 (Stall, MemRead_EX, or_1_out);
endmodule
