// Logisim project OpCodeDecoder.circ as structural Verilog: 1 circuit, main circuit main
module main (
);

  wire ADD, ADDI, AND, ANDI, BEQ, BGE, BGEU, BLT, BLTU, BNE, decoder_1_out0, JALR, LW, MUL, NOR, NORI, OR,
       ORI, ROR, RORI, SEQ, SEQI, SET, SLL, SLLI, SLT, SLTI, SLTIU, SLTU, SRA, SRAI, SRL, SRLI, SSET, SUB,
       SW, XOR, XORI;
  wire [3:0] Funct;
  wire [4:0] OP;

  Decoder #(.select(5), .enable("false")) decoder_1 (
    .out0(decoder_1_out0), .out1(SLLI), .out2(SRLI), .out3(SRAI), .out4(RORI), .out5(ADDI), .out6(SLTI),
    .out7(SLTIU), .out8(SEQI), .out9(XORI), .out10(ORI), .out11(ANDI), .out12(NORI), .out13(SET),
    .out14(SSET), .out15(JALR), .out16(LW), .out17(SW), .out18(BEQ), .out19(BNE), .out20(BLT), .out21(BGE),
    .out22(BLTU), .out23(BGEU), .sel(OP));  // open: out24, out25, out26, out27, out28, out29, out30, out31
  Decoder #(.select(4)) decoder_2 (
    .out0(SLL), .out1(SRL), .out2(SRA), .out3(ROR), .out4(ADD), .out5(SUB), .out6(SLT), .out7(SLTU),
    .out8(SEQ), .out9(XOR), .out10(OR), .out11(AND), .out12(NOR), .out13(MUL), .sel(Funct),
    .en(decoder_1_out0));  // open: out14, out15

  // Notes on the sheet:
  //   Op=0
endmodule
