// Logisim project RF.circ as structural Verilog
module Reg_file (
  input  [4:0] in_1,
  input  [4:0] RW,
  input  [4:0] in_3,
  input  clock,
  input  Reg_Write,
  input  [31:0] DATA_IN,
  output [31:0] out_7,
  output [31:0] out_8,
  output [31:0] out_9,
  output [31:0] out_10,
  output [31:0] out_11,
  output [31:0] out_12,
  output [31:0] out_13,
  output [31:0] out_14,
  output [31:0] out_15,
  output [31:0] out_16,
  output [31:0] out_17,
  output [31:0] out_18,
  output [31:0] out_19,
  output [31:0] out_20,
  output [31:0] out_21,
  output [31:0] out_22,
  output [31:0] out_23,
  output [31:0] out_24,
  output [31:0] out_25,
  output [31:0] out_26,
  output [31:0] out_27,
  output [31:0] out_28,
  output [31:0] out_29,
  output [31:0] out_30,
  output [31:0] out_31,
  output [31:0] out_32,
  output [31:0] out_33,
  output [31:0] out_34,
  output [31:0] out_35,
  output [31:0] out_36,
  output [31:0] out_37,
  output [31:0] out_38,
  output [31:0] out_39,
  output [31:0] out_40
);

  wire and_1_out, and_2_out, and_3_out, and_4_out, and_5_out, and_6_out, and_7_out, and_8_out, and_9_out,
       and_10_out, and_11_out, and_12_out, and_13_out, and_14_out, and_15_out, and_16_out, and_17_out,
       and_18_out, and_19_out, and_20_out, and_21_out, and_22_out, and_23_out, and_24_out, and_25_out,
       and_26_out, and_27_out, and_28_out, and_29_out, and_30_out, and_31_out, and_32_out, decoder_1_out0,
       decoder_1_out1, decoder_1_out2, decoder_1_out3, decoder_1_out4, decoder_1_out5, decoder_1_out6,
       decoder_1_out7, decoder_1_out8, decoder_1_out9, decoder_1_out10, decoder_1_out11, decoder_1_out12,
       decoder_1_out13, decoder_1_out14, decoder_1_out15, decoder_1_out16, decoder_1_out17, decoder_1_out18,
       decoder_1_out19, decoder_1_out20, decoder_1_out21, decoder_1_out22, decoder_1_out23, decoder_1_out24,
       decoder_1_out25, decoder_1_out26, decoder_1_out27, decoder_1_out28, decoder_1_out29, decoder_1_out30,
       decoder_1_out31;

  Decoder #(.select(5), .enable("false")) decoder_1 (
    .out0(decoder_1_out0), .out1(decoder_1_out1), .out2(decoder_1_out2), .out3(decoder_1_out3),
    .out4(decoder_1_out4), .out5(decoder_1_out5), .out6(decoder_1_out6), .out7(decoder_1_out7),
    .out8(decoder_1_out8), .out9(decoder_1_out9), .out10(decoder_1_out10), .out11(decoder_1_out11),
    .out12(decoder_1_out12), .out13(decoder_1_out13), .out14(decoder_1_out14), .out15(decoder_1_out15),
    .out16(decoder_1_out16), .out17(decoder_1_out17), .out18(decoder_1_out18), .out19(decoder_1_out19),
    .out20(decoder_1_out20), .out21(decoder_1_out21), .out22(decoder_1_out22), .out23(decoder_1_out23),
    .out24(decoder_1_out24), .out25(decoder_1_out25), .out26(decoder_1_out26), .out27(decoder_1_out27),
    .out28(decoder_1_out28), .out29(decoder_1_out29), .out30(decoder_1_out30), .out31(decoder_1_out31),
    .sel(RW));
  and and_1 (and_1_out, decoder_1_out0, Reg_Write);
  and and_2 (and_2_out, decoder_1_out1, Reg_Write);
  and and_3 (and_3_out, decoder_1_out2, Reg_Write);
  and and_4 (and_4_out, decoder_1_out3, Reg_Write);
  and and_5 (and_5_out, decoder_1_out4, Reg_Write);
  and and_6 (and_6_out, decoder_1_out5, Reg_Write);
  and and_7 (and_7_out, decoder_1_out6, Reg_Write);
  and and_8 (and_8_out, decoder_1_out7, Reg_Write);
  and and_9 (and_9_out, decoder_1_out8, Reg_Write);
  and and_10 (and_10_out, decoder_1_out9, Reg_Write);
  and and_11 (and_11_out, decoder_1_out10, Reg_Write);
  and and_12 (and_12_out, decoder_1_out11, Reg_Write);
  and and_13 (and_13_out, decoder_1_out12, Reg_Write);
  and and_14 (and_14_out, decoder_1_out13, Reg_Write);
  and and_15 (and_15_out, decoder_1_out14, Reg_Write);
  and and_16 (and_16_out, decoder_1_out15, Reg_Write);
  and and_17 (and_17_out, decoder_1_out16, Reg_Write);
  and and_18 (and_18_out, decoder_1_out17, Reg_Write);
  and and_19 (and_19_out, decoder_1_out18, Reg_Write);
  and and_20 (and_20_out, decoder_1_out19, Reg_Write);
  and and_21 (and_21_out, decoder_1_out20, Reg_Write);
  and and_22 (and_22_out, decoder_1_out21, Reg_Write);
  and and_23 (and_23_out, decoder_1_out22, Reg_Write);
  and and_24 (and_24_out, decoder_1_out23, Reg_Write);
  and and_25 (and_25_out, decoder_1_out24, Reg_Write);
  and and_26 (and_26_out, decoder_1_out25, Reg_Write);
  and and_27 (and_27_out, decoder_1_out26, Reg_Write);
  and and_28 (and_28_out, decoder_1_out27, Reg_Write);
  and and_29 (and_29_out, decoder_1_out28, Reg_Write);
  and and_30 (and_30_out, decoder_1_out29, Reg_Write);
  and and_31 (and_31_out, decoder_1_out30, Reg_Write);
  and and_32 (and_32_out, decoder_1_out31, Reg_Write);
  Register #(.width(32)) register_1 (.D(DATA_IN), .en(and_13_out), .clk(clock), .Q(out_21));  // open: clr
  Register #(.width(32)) register_2 (.D(DATA_IN), .en(and_15_out), .clk(clock), .Q(out_23));  // open: clr
  Register #(.width(32)) register_3 (.D(DATA_IN), .en(and_17_out), .clk(clock), .Q(out_25));  // open: clr
  Register #(.width(32)) register_4 (.D(DATA_IN), .en(and_19_out), .clk(clock), .Q(out_27));  // open: clr
  Register #(.width(32)) register_5 (.D(DATA_IN), .en(and_21_out), .clk(clock), .Q(out_30));  // open: clr
  Register #(.width(32)) register_6 (.D(DATA_IN), .en(and_23_out), .clk(clock), .Q(out_31));  // open: clr
  Register #(.width(32)) register_7 (.D(DATA_IN), .en(and_25_out), .clk(clock), .Q(out_33));  // open: clr
  Register #(.width(32)) register_8 (.D(DATA_IN), .en(and_27_out), .clk(clock), .Q(out_36));  // open: clr
  Register #(.width(32)) register_9 (.D(DATA_IN), .en(and_29_out), .clk(clock), .Q(out_38));  // open: clr
  Register #(.width(32)) register_10 (.D(DATA_IN), .en(and_31_out), .clk(clock), .Q(out_40), .clr(and_32_out));
  Register #(.width(32)) register_11 (.D({32{1'b0}}), .en(and_1_out), .clk(clock), .Q(out_7));  // open: clr
  Register #(.width(32)) register_12 (.D(DATA_IN), .en(and_3_out), .clk(clock), .Q(out_9));  // open: clr
  Register #(.width(32)) register_13 (.D(DATA_IN), .en(and_5_out), .clk(clock), .Q(out_11));  // open: clr
  Register #(.width(32)) register_14 (.D(DATA_IN), .en(and_7_out), .clk(clock), .Q(out_14));  // open: clr
  Register #(.width(32)) register_15 (.D(DATA_IN), .en(and_9_out), .clk(clock), .Q(out_15));  // open: clr
  Register #(.width(32)) register_16 (.D(DATA_IN), .en(and_11_out), .clk(clock), .Q(out_18));  // open: clr
  Register #(.width(32)) register_17 (.D(DATA_IN), .en(and_14_out), .clk(clock), .Q(out_20));  // open: clr
  Register #(.width(32)) register_18 (.D(DATA_IN), .en(and_16_out), .clk(clock), .Q(out_22));  // open: clr
  Register #(.width(32)) register_19 (.D(DATA_IN), .en(and_18_out), .clk(clock), .Q(out_24));  // open: clr
  Register #(.width(32)) register_20 (.D(DATA_IN), .en(and_20_out), .clk(clock), .Q(out_26));  // open: clr
  Register #(.width(32)) register_21 (.D(DATA_IN), .en(and_22_out), .clk(clock), .Q(out_28));  // open: clr
  Register #(.width(32)) register_22 (.D(DATA_IN), .en(and_24_out), .clk(clock), .Q(out_32));  // open: clr
  Register #(.width(32)) register_23 (.D(DATA_IN), .en(and_26_out), .clk(clock), .Q(out_34));  // open: clr
  Register #(.width(32)) register_24 (.D(DATA_IN), .en(and_28_out), .clk(clock), .Q(out_35));  // open: clr
  Register #(.width(32)) register_25 (.D(DATA_IN), .en(and_30_out), .clk(clock), .Q(out_37));  // open: clr
  Register #(.width(32)) register_26 (.D(DATA_IN), .en(and_32_out), .clk(clock), .Q(out_39));  // open: clr
  Register #(.width(32)) register_27 (.D(DATA_IN), .en(and_2_out), .clk(clock), .Q(out_8));  // open: clr
  Register #(.width(32)) register_28 (.D(DATA_IN), .en(and_4_out), .clk(clock), .Q(out_10));  // open: clr
  Register #(.width(32)) register_29 (.D(DATA_IN), .en(and_6_out), .clk(clock), .Q(out_12));  // open: clr
  Register #(.width(32)) register_30 (.D(DATA_IN), .en(and_8_out), .clk(clock), .Q(out_13));  // open: clr
  Register #(.width(32)) register_31 (.D(DATA_IN), .en(and_10_out), .clk(clock), .Q(out_16));  // open: clr
  Register #(.width(32)) register_32 (.D(DATA_IN), .en(and_12_out), .clk(clock), .Q(out_17));  // open: clr
  Multiplexer #(.select(5), .width(32), .enable("false")) multiplexer_1 (
    .in0(out_7), .in1(out_8), .in2(out_9), .in3(out_10), .in4(out_11), .in5(out_12), .in6(out_14),
    .in7(out_13), .in8(out_15), .in9(out_16), .in10(out_18), .in11(out_17), .in12(out_21), .in13(out_20),
    .in14(out_23), .in15(out_22), .in16(out_25), .in17(out_24), .in18(out_27), .in19(out_26), .in20(out_30),
    .in21(out_28), .in22(out_31), .in23(out_32), .in24(out_33), .in25(out_34), .in26(out_36), .in27(out_35),
    .in28(out_38), .in29(out_37), .in30(out_40), .in31(out_39), .out(out_29), .sel(in_3));
  Multiplexer #(.select(5), .width(32), .enable("false")) multiplexer_2 (
    .in0(out_7), .in1(out_8), .in2(out_9), .in3(out_10), .in4(out_11), .in5(out_12), .in6(out_14),
    .in7(out_13), .in8(out_15), .in9(out_16), .in10(out_18), .in11(out_17), .in12(out_21), .in13(out_20),
    .in14(out_23), .in15(out_22), .in16(out_25), .in17(out_24), .in18(out_27), .in19(out_26), .in20(out_30),
    .in21(out_28), .in22(out_31), .in23(out_32), .in24(out_33), .in25(out_34), .in26(out_36), .in27(out_35),
    .in28(out_38), .in29(out_37), .in30(out_40), .in31(out_39), .out(out_19), .sel(in_1));

  // Other names for the same wires on the sheet: R0[31:0] = out_7; R1[31:0] = out_8; R2[31:0] = out_9;
  //   R3[31:0] = out_10; R4[31:0] = out_11; R5[31:0] = out_12; R6[31:0] = out_14; R7[31:0] = out_13;
  //   R8[31:0] = out_15; R9[31:0] = out_16; R10[31:0] = out_18; R11[31:0] = out_17; R12[31:0] = out_21;
  //   R13[31:0] = out_20; R14[31:0] = out_23; R15[31:0] = out_22; R16[31:0] = out_25; R17[31:0] = out_24;
  //   R18[31:0] = out_27; R19[31:0] = out_26; R20[31:0] = out_30; R21[31:0] = out_28; R22[31:0] = out_31;
  //   R23[31:0] = out_32; R24[31:0] = out_33; R25[31:0] = out_34; R26[31:0] = out_36; R27[31:0] = out_35;
  //   R28[31:0] = out_38; R29[31:0] = out_37; R30[31:0] = out_40; R31[31:0] = out_39
endmodule
