// Logisim project data_mem.circ as structural Verilog: 1 circuit, main circuit main
module main (
  input  [31:0] in_1,
  input  in_2,
  input  in_3,
  input  in_4
);

  wire jalr, mem_to_reg;
  wire [19:0] pc_inc;
  wire [31:0] ALU_result, bit_extender_1_out, BusB, BusW, multiplexer_1_out, ram_1_dout;

  // Probe on in_1[19:0]
  RAM #(.addrWidth(20), .dataWidth(32), .databus("bibus")) ram_1 (
    .addr(in_1[19:0]), .we(in_2), .oe(in_3), .clk(in_4), .din(BusB), .dout(ram_1_dout));
  // Probe on in_1[19:0]
  // Probe on ram_1_dout
  Multiplexer #(.width(32), .enable("false")) multiplexer_1 (
    .in0(ram_1_dout), .in1(ALU_result), .out(multiplexer_1_out), .sel(mem_to_reg));
  assign bit_extender_1_out = {{12{1'b0}}, pc_inc};  // Bit_Extender bit_extender_1
  Multiplexer #(.width(32), .enable("false")) multiplexer_2 (
    .in0(multiplexer_1_out), .in1(bit_extender_1_out), .out(BusW), .sel(jalr));
  // Probe on BusW
endmodule
