// Logisim project instruction_mem.circ as structural Verilog: 1 circuit, main circuit main
module main (
  input  [19:0] in_1,
  output [31:0] out_2
);

  ROM #(.addrWidth(20), .dataWidth(32)) rom_1 (.addr(in_1), .data(out_2));

  // Other names for the same wires on the sheet: instruction[31:0] = out_2; pc[19:0] = in_1

  // Notes on the sheet:
  //   contents of rom_1 (hex, n*v repeats v):
  //   221acd2 122ca 123459 155cab 12bcd 222cd
endmodule
